# Fritzing sketch IR_esp8266 (saved by Fritzing 0.9.3b)

parts:
  WeMos_D1_Mini2 = WeMos D1 Mini
  Power_5_5x2_1 = Power 5.5x2.5
  IR1 = TSOP312.., 314.. [package=THT]

nets:
  N1: WeMos_D1_Mini2.5V, Power_5_5x2_1.PWR
  N2: WeMos_D1_Mini2.D4, IR1.GND
  N3: WeMos_D1_Mini2.G, Power_5_5x2_1.GND
